// Digital circuit 4Way16Mux (2023-06-03).dig as structural Verilog
module _4Way16Mux__2023_06_03 (
  input  [15:0] in_2,
  input  [15:0] in_3,
  input  [15:0] in_4,
  input  [15:0] in_5,
  input  in_6,
  input  in_7,
  output [15:0] out_1
);

  wire [15:0] multiplexer_1_out, multiplexer_2_out;

  Multiplexer #(.Bits(16)) multiplexer_1 (.sel(in_6), .in_0(in_2), .in_1(in_3), .out(multiplexer_1_out));
  Multiplexer #(.Bits(16)) multiplexer_2 (.sel(in_6), .in_0(in_4), .in_1(in_5), .out(multiplexer_2_out));
  Multiplexer #(.Bits(16)) multiplexer_3 (.sel(in_7), .in_0(multiplexer_1_out), .in_1(multiplexer_2_out), .out(out_1));
endmodule
