// Digital circuit 4Way16Mux.dig as structural Verilog
module _4Way16Mux (
  input  [15:0] a,
  input  [15:0] b,
  input  [15:0] c,
  input  [15:0] d,
  input  sel1,
  input  sel2,
  output [15:0] out_7
);

  wire not_1_out, not_2_out, not_3_out, not_4_out;
  wire [15:0] and_1_out, and_2_out, and_3_out, and_4_out, and_5_out, and_6_out, and_7_out, and_8_out,
       or_1_out, or_2_out;

  not not_1 (not_1_out, sel1);
  not not_2 (not_2_out, sel1);
  not not_3 (not_3_out, sel2);
  and and_1 (and_1_out[0], not_1_out, sel2);
  not not_4 (not_4_out, sel1);
  and and_2 (and_2_out[0], not_2_out, not_3_out);
  and and_3 (and_3_out[0], sel2, not_4_out);
  and and_4 (and_4_out[0], sel1, sel2);
  assign and_5_out = and_2_out & a;  // And and_5, 16 bits wide
  assign and_6_out = b & and_1_out;  // And and_6, 16 bits wide
  assign and_7_out = and_3_out & c;  // And and_7, 16 bits wide
  assign and_8_out = and_4_out & d;  // And and_8, 16 bits wide
  assign or_1_out = and_5_out | and_6_out;  // Or or_1, 16 bits wide
  assign or_2_out = and_7_out | and_8_out;  // Or or_2, 16 bits wide
  assign out_7 = or_1_out | or_2_out;  // Or or_3, 16 bits wide
  // Pins of 1 and 16 bits meet at and_2_out
  // Pins of 1 and 16 bits meet at and_1_out
  // Pins of 1 and 16 bits meet at and_3_out
  // Pins of 1 and 16 bits meet at and_4_out
endmodule
