// Digital circuit 4WayDMUX (2023-06-02).dig as structural Verilog
module _4WayDMUX__2023_06_02 (
  input  in_5,
  input  [1:0] InA,
  output out_1,
  output out_2,
  output out_3,
  output out_4
);

  wire and_1_out, and_2_out, and_3_out, and_4_out, not_1_out, not_2_out, not_3_out, not_4_out;

  not not_1 (not_1_out, InA[0]);
  not not_2 (not_2_out, InA[1]);
  not not_3 (not_3_out, InA[1]);
  not not_4 (not_4_out, InA[0]);
  and and_1 (and_1_out, not_1_out, not_2_out);
  and and_2 (and_2_out, InA[0], not_3_out);
  and and_3 (and_3_out, not_4_out, InA[1]);
  and and_4 (and_4_out, InA[0], InA[1]);
  and and_5 (out_1, and_1_out, in_5);
  and and_6 (out_2, and_2_out, in_5);
  and and_7 (out_3, and_3_out, in_5);
  and and_8 (out_4, and_4_out, in_5);
endmodule
