// Digital circuit 4WayDMux (2023-06-03).dig as structural Verilog
module _4WayDMux__2023_06_03 (
  input  in_5,
  input  _1,
  input  _0,
  output out_1,
  output out_2,
  output out_3,
  output out_4
);

  wire demultiplexer_1_out_0, demultiplexer_1_out_1;

  Demultiplexer demultiplexer_1 (.sel(_1), .in(in_5), .out_0(demultiplexer_1_out_0), .out_1(demultiplexer_1_out_1));
  Demultiplexer demultiplexer_2 (.sel(_0), .in(demultiplexer_1_out_0), .out_0(out_1), .out_1(out_2));
  Demultiplexer demultiplexer_3 (.sel(_0), .in(demultiplexer_1_out_1), .out_0(out_3), .out_1(out_4));
endmodule
