// Digital circuit 8WayDMux (2023-06-03).dig as structural Verilog
module _8WayDMux__2023_06_03 (
  input  in_5,
  input  _1,
  input  _2,
  input  _0,
  output out_1,
  output out_2,
  output out_3,
  output out_4,
  output out_8,
  output out_9,
  output out_10,
  output out_11
);

  wire demultiplexer_1_out_0, demultiplexer_1_out_1;

  Demultiplexer demultiplexer_1 (.sel(_2), .in(in_5), .out_0(demultiplexer_1_out_0), .out_1(demultiplexer_1_out_1));
  Demultiplexer #(.Selector_Bits(2)) demultiplexer_2 (
    .sel({_1, _0}), .in(demultiplexer_1_out_0), .out_0(out_1), .out_1(out_2), .out_2(out_3), .out_3(out_4));
  Demultiplexer #(.Selector_Bits(2)) demultiplexer_3 (
    .sel({_1, _0}), .in(demultiplexer_1_out_1), .out_0(out_8), .out_1(out_9), .out_2(out_10), .out_3(out_11));
endmodule
