// Digital circuit 8WayOR.dig as structural Verilog
module _8WayOR (
);

  wire or_1_out, or_2_out, or_3_out, or_4_out, or_5_out, or_6_out;

  // Or or_1 has open pins: In_1=open, In_2=open, out=or_1_out
  // Or or_2 has open pins: In_1=open, In_2=open, out=or_2_out
  // Or or_3 has open pins: In_1=open, In_2=open, out=or_3_out
  // Or or_4 has open pins: In_1=open, In_2=open, out=or_4_out
  or or_5 (or_5_out, or_1_out, or_2_out);
  or or_6 (or_6_out, or_3_out, or_4_out);
  // Or or_7 has open pins: In_1=or_5_out, In_2=or_6_out, out=open
endmodule
