// Digital circuit ALU (2023-06-06).dig as structural Verilog
module ALU__2023_06_06 (
  input  [15:0] x,
  input  [15:0] y,
  input  zx,
  input  zy,
  input  f,
  input  no,
  input  nx,
  input  ny,
  output [15:0] out,
  output zr,
  output ng
);

  wire or_1_out, or_2_out, or_3_out, or_4_out, or_5_out, or_6_out, or_7_out, or_8_out, or_9_out, or_10_out,
       or_11_out, or_12_out, or_13_out, or_14_out, or_15_out;
  wire [15:0] add_1_s, and_1_out, multiplexer_1_out, multiplexer_2_out, multiplexer_5_out, not_1_out,
       not_2_out, not_3_out, readyX, readyY;

  Multiplexer #(.Bits(16)) multiplexer_1 (.sel(zx), .in_0(x), .in_1({16{1'b0}}), .out(multiplexer_1_out));
  assign not_1_out = ~multiplexer_1_out;  // Not not_1, 16 bits wide
  Multiplexer #(.Bits(16)) multiplexer_2 (.sel(zy), .in_0(y), .in_1({16{1'b0}}), .out(multiplexer_2_out));
  Multiplexer #(.Bits(16)) multiplexer_3 (.sel(ny), .in_0(multiplexer_2_out), .in_1(not_2_out), .out(readyY));
  assign not_2_out = ~multiplexer_2_out;  // Not not_2, 16 bits wide
  Multiplexer #(.Bits(16)) multiplexer_4 (.sel(nx), .in_0(multiplexer_1_out), .in_1(not_1_out), .out(readyX));
  or or_1 (or_1_out, out[0], out[1]);
  or or_2 (or_2_out, out[2], out[3]);
  or or_3 (or_3_out, out[4], out[5]);
  or or_4 (or_4_out, out[6], out[7]);
  or or_5 (or_5_out, out[8], out[9]);
  or or_6 (or_6_out, out[10], out[11]);
  or or_7 (or_7_out, out[12], out[13]);
  or or_8 (or_8_out, out[14], ng);
  or or_9 (or_9_out, or_3_out, or_4_out);
  or or_10 (or_10_out, or_5_out, or_6_out);
  or or_11 (or_11_out, or_7_out, or_8_out);
  or or_12 (or_12_out, or_1_out, or_2_out);
  assign and_1_out = readyX & readyY;  // And and_1, 16 bits wide
  Add #(.Bits(16)) add_1 (.a(readyX), .b(readyY), .c_i(1'b0), .s(add_1_s));  // open: c_o
  or or_13 (or_13_out, or_12_out, or_9_out);
  or or_14 (or_14_out, or_10_out, or_11_out);
  Multiplexer #(.Bits(16)) multiplexer_5 (.sel(f), .in_0(and_1_out), .in_1(add_1_s), .out(multiplexer_5_out));
  or or_15 (or_15_out, or_13_out, or_14_out);
  assign not_3_out = ~multiplexer_5_out;  // Not not_3, 16 bits wide
  not not_4 (zr, or_15_out);
  Multiplexer #(.Bits(16)) multiplexer_6 (.sel(no), .in_0(multiplexer_5_out), .in_1(not_3_out), .out({ng, out[14:0]}));
  // Pins of 1 and 16 bits meet at {16{1'b0}}

  assign out[15] = ng;

  // Other names for the same wires on the sheet: readyOut[15:0] = {ng, out[14:0]}

  // Notes on the sheet:
  //   Flags
endmodule
