// Digital circuit AND(4-bit).dig as structural Verilog
module AND_4_bit (
  input  [1:0] a,
  input  [1:0] b,
  output [1:0] Out
);

  wire [1:0] nand_1_out;

  assign nand_1_out = ~(a & b);  // NAnd nand_1, 2 bits wide
  assign Out = ~nand_1_out;  // Not not_1, 2 bits wide
endmodule
