// Digital circuit AndGate.dig as structural Verilog
module AndGate (
  input  In,
  input  In_2,
  output Out
);

  wire nand_1_out;

  nand nand_1 (nand_1_out, In, In_2);
  not not_1 (Out, nand_1_out);
endmodule
