// Digital circuit DMuxGate.dig as structural Verilog
module DMuxGate (
  input  in_3,
  input  in_4,
  output out_1,
  output out_2
);

  wire not_1_out, or_1_out;

  or or_1 (or_1_out, in_3, in_4);
  not not_1 (not_1_out, in_4);
  and and_1 (out_1, or_1_out, not_1_out);
  and and_2 (out_2, in_3, in_4);
endmodule
