// Digital circuit FullAdder (2023-06-05).dig as structural Verilog
module FullAdder__2023_06_05 (
  input  a__MSB,
  input  c__LSB,
  input  b,
  output carry,
  output sum
);

  wire half_adder__2023_06_05_1_carry, half_adder__2023_06_05_1_sum, half_adder__2023_06_05_2_carry;

  Half_Adder__2023_06_05 half_adder__2023_06_05_1 (
    .a(a__MSB), .b(b), .carry(half_adder__2023_06_05_1_carry), .sum(half_adder__2023_06_05_1_sum));
  Half_Adder__2023_06_05 half_adder__2023_06_05_2 (
    .a(half_adder__2023_06_05_1_sum), .b(c__LSB), .carry(half_adder__2023_06_05_2_carry), .sum(sum));
  or or_1 (carry, half_adder__2023_06_05_1_carry, half_adder__2023_06_05_2_carry);
endmodule
