// Digital circuit Half-Adder (2023-06-05).dig as structural Verilog
module Half_Adder__2023_06_05 (
  input  a,
  input  b,
  output carry,
  output sum
);

  xor xor_1 (sum, a, b);
  and and_1 (carry, a, b);
endmodule
