// Digital circuit HalfAdderChip.dig as structural Verilog
module HalfAdderChip (
  input  a,
  input  b,
  output sum,
  output carry
);

  xor xor_1 (sum, a, b);
  and and_1 (carry, a, b);
endmodule
