// Digital circuit MUX (2023-05-31).dig as structural Verilog
module MUX__2023_05_31 (
  input  in_2,
  input  in_3,
  input  in_4,
  output out_1
);

  wire and_1_out, and_2_out, and_3_out, not_1_out, or_1_out;

  and and_1 (and_1_out, in_3, in_4);
  not not_1 (not_1_out, in_4);
  and and_2 (and_2_out, in_2, not_1_out);
  and and_3 (and_3_out, in_2, in_3);
  or or_1 (or_1_out, and_2_out, and_1_out);
  or or_2 (out_1, and_3_out, or_1_out);
endmodule
