// Digital circuit MuxGate.dig as structural Verilog
module MuxGate (
  input  a,
  input  b,
  input  sel,
  output out_4
);

  wire not_1_out, or_1_out, or_2_out;

  not not_1 (not_1_out, sel);
  or or_1 (or_1_out, a, sel);
  or or_2 (or_2_out, b, not_1_out);
  and and_1 (out_4, or_1_out, or_2_out);
endmodule
