// Digital circuit Not (2023-05-30).dig as structural Verilog
module Not__2023_05_30 (
  input  in_1,
  input  in_3,
  output out_2
);

  wire nand_1_out;

  nand nand_1 (nand_1_out, in_1, in_3);
  not not_1 (out_2, nand_1_out);
endmodule
