// Digital circuit OR (2023-05-30).dig as structural Verilog
module OR__2023_05_30 (
  input  in_1,
  input  in_2,
  output out_3
);

  wire not_1_out, not_2_out;

  not not_1 (not_1_out, in_1);
  not not_2 (not_2_out, in_2);
  nand nand_1 (out_3, not_1_out, not_2_out);
endmodule
