// Digital circuit Or Gate.dig as structural Verilog
module Or_Gate (
  input  IN_A,
  input  In_B,
  output Out_C
);

  wire not_1_out, not_2_out;

  not not_1 (not_1_out, IN_A);
  not not_2 (not_2_out, In_B);
  nand nand_1 (Out_C, not_1_out, not_2_out);
endmodule
