// Digital circuit Ram64.dig as structural Verilog
module Ram64 (
  input  [15:0] in,
  input  [5:0] selector,
  input  load,
  output [15:0] out
);

  wire [15:0] _0_out, _1_out, _2_out, _3_out, _4_out, _5_p2, _6_out, _7_out;

  Demultiplexer #(.Selector_Bits(3)) demultiplexer_1 (.in(load));  // open: sel, out_0, out_1, out_2, out_3, out_4, out_5, out_6, out_7
  Ram8__2023_06_10 _0 (.in(in), .address(selector[5:3]), .out(_0_out));  // open: clock, load
  Ram8__2023_06_10 _1 (.in(in), .address(selector[5:3]), .out(_1_out));  // open: clock, load
  Ram8__2023_06_10 _2 (.in(in), .address(selector[5:3]), .out(_2_out));  // open: clock, load
  Ram8__2023_06_10 _3 (.in(in), .address(selector[5:3]), .out(_3_out));  // open: clock, load
  Ram8__2023_06_10 _4 (.in(in), .address(selector[5:3]), .out(_4_out));  // open: clock, load
  // Ram8__2023_06_10 _5: pin names not known; wires that end beside it: selector[5:3], _5_p2
  Ram8__2023_06_10 _6 (.in(in), .address(selector[5:3]), .out(_6_out));  // open: clock, load
  Ram8__2023_06_10 _7 (.in(in), .address(selector[5:3]), .out(_7_out));  // open: clock, load
  Multiplexer #(.Bits(16), .Selector_Bits(3)) multiplexer_1 (
    .sel(selector[2:0]), .in_0(_0_out), .in_1(_1_out), .in_2(_2_out), .in_3(_3_out), .in_4(_4_out),
    .in_5(_5_p2), .in_6(_6_out), .in_7(_7_out), .out(out));
endmodule
