// Digital circuit Ram8 (2023-06-10).dig as structural Verilog
module Ram8__2023_06_10 (
  input  [15:0] in,
  input  [2:0] address,
  input  clock,
  input  load,
  output [15:0] out
);

  wire demultiplexer_1_out_0, demultiplexer_1_out_1, demultiplexer_1_out_2, demultiplexer_1_out_3,
       demultiplexer_1_out_4, demultiplexer_1_out_5, demultiplexer_1_out_6, demultiplexer_1_out_7;
  wire [15:0] _0_q, _1_q, _2_q, _3_q, _4_q, _5_q, _6_q, _7_q;

  Demultiplexer #(.Selector_Bits(3)) demultiplexer_1 (
    .sel(address), .in(load), .out_0(demultiplexer_1_out_0), .out_1(demultiplexer_1_out_1),
    .out_2(demultiplexer_1_out_2), .out_3(demultiplexer_1_out_3), .out_4(demultiplexer_1_out_4),
    .out_5(demultiplexer_1_out_5), .out_6(demultiplexer_1_out_6), .out_7(demultiplexer_1_out_7));
  Register #(.Bits(16)) _0 (.D(in), .C(clock), .en(demultiplexer_1_out_0), .Q(_0_q));
  Register #(.Bits(16)) _1 (.D(in), .C(clock), .en(demultiplexer_1_out_1), .Q(_1_q));
  Register #(.Bits(16)) _2 (.D(in), .C(clock), .en(demultiplexer_1_out_2), .Q(_2_q));
  Register #(.Bits(16)) _3 (.D(in), .C(clock), .en(demultiplexer_1_out_3), .Q(_3_q));
  Register #(.Bits(16)) _4 (.D(in), .C(clock), .en(demultiplexer_1_out_4), .Q(_4_q));
  Register #(.Bits(16)) _5 (.D(in), .C(clock), .en(demultiplexer_1_out_5), .Q(_5_q));
  Register #(.Bits(16)) _6 (.D(in), .C(clock), .en(demultiplexer_1_out_6), .Q(_6_q));
  Register #(.Bits(16)) _7 (.D(in), .C(clock), .en(demultiplexer_1_out_7), .Q(_7_q));
  Multiplexer #(.Bits(16), .Selector_Bits(3)) multiplexer_1 (
    .sel(address), .in_0(_0_q), .in_1(_1_q), .in_2(_2_q), .in_3(_3_q), .in_4(_4_q), .in_5(_5_q), .in_6(_6_q),
    .in_7(_7_q), .out(out));
endmodule
