// Digital circuit Ram8.dig as structural Verilog
module Ram8 (
  input  in_1,
  input  [2:0] in_2,
  input  clk,
  input  load,
  output out_5
);

  wire [15:0] demultiplexer_1_out_0, demultiplexer_1_out_1, demultiplexer_1_out_2, demultiplexer_1_out_3,
       demultiplexer_1_out_4, demultiplexer_1_out_5, demultiplexer_1_out_6, demultiplexer_1_out_7;

  Demultiplexer #(.Bits(16), .Selector_Bits(3)) demultiplexer_1 (
    .sel(in_2), .out_0(demultiplexer_1_out_0), .out_1(demultiplexer_1_out_1), .out_2(demultiplexer_1_out_2),
    .out_3(demultiplexer_1_out_3), .out_4(demultiplexer_1_out_4), .out_5(demultiplexer_1_out_5),
    .out_6(demultiplexer_1_out_6), .out_7(demultiplexer_1_out_7));  // open: in
  Register #(.Bits(16)) _1 (.D(demultiplexer_1_out_0), .C(clk), .en(load));  // open: Q
  Register register_1 (.D(demultiplexer_1_out_1[0]), .C(clk), .en(load));  // open: Q
  // Pins of 1 and 16 bits meet at demultiplexer_1_out_1
endmodule
