// Digital circuit XOR (2023-05-30).dig as structural Verilog
module XOR__2023_05_30 (
  input  in_1,
  input  in_2,
  output out_3
);

  wire and_1_out, and_2_out, not_1_out, not_2_out;

  not not_1 (not_1_out, in_2);
  not not_2 (not_2_out, in_1);
  and and_1 (and_1_out, in_1, not_1_out);
  and and_2 (and_2_out, not_2_out, in_2);
  or or_1 (out_3, and_1_out, and_2_out);
endmodule
